# Fritzing sketch first_mb_proto (saved by Fritzing 0.8.7b)
circuit board: 5.64444cm x 8.46667cm
perfboards: 1

parts:
  S1 = Momentary Switch [package=ksa_sealed_tac_switch]
  Y1 = CRYSTAL [package=crystal-smd-10.5x4.8-2pin]
  Nokia_5110_LCD_Module1 = Nokia5110LCDModule
  U1 = atmega328 [package=dip]
  R1 = Resistor [tolerance=±5% resistance=10k package=THT]
  U2 = Vibration Motor- ROB-08449 [package=vibe-motor-10mm]
  S2 = Momentary Switch [package=ksa_sealed_tac_switch]
  S3 = Momentary Switch [package=ksa_sealed_tac_switch]
  S4 = Momentary Switch [package=ksa_sealed_tac_switch]
  S5 = Momentary Switch [package=ksa_sealed_tac_switch]
  S6 = Momentary Switch [package=ksa_sealed_tac_switch]
  LED1 = LED - 3mm [color="Red (660nm)" package="3 mm [THT]"]
  J1 = female pin header, 6 pins [form="♀ (female)"]
  S7 = Momentary Switch [package=ksa_sealed_tac_switch]
  R2 = Resistor [tolerance=±5% resistance=220 package=THT]
  C1 = Ceramic Capacitor [capacitance=2.2µF package="100 mil [THT, multilayer]"]
  C2 = Ceramic Capacitor [capacitance=2.2µF package="100 mil [THT, multilayer]"]
  R3 = Resistor [tolerance=±5% resistance=10k package=THT]
  U3 = Ebay Breakout Board for SD Cards

nets:
  N1: S1.2, U1.D6_(PWM)
  N2: Y1.1, U1.XLAT2, C2.1
  N3: Y1.2, U1.D5_(PWM), C1.0
  N4: Nokia_5110_LCD_Module1.Vcc, U1.A0
  N5: Nokia_5110_LCD_Module1.Grnd, U1.A1
  N6: Nokia_5110_LCD_Module1.SCE, U1.A2
  N7: Nokia_5110_LCD_Module1.RST, U1.D11_(PWM), U3.MOSI
  N8: Nokia_5110_LCD_Module1.D/C, U1.D13, R1.Pin_0, U3.SCK
  N9: Nokia_5110_LCD_Module1.6_DN_(MOSI), Nokia_5110_LCD_Module1.SCLK, U1.VCC, U1.AREF, R1.Pin_1, R3.Pin_1
  GND: Nokia_5110_LCD_Module1.LED, U1.GND, U2.+, LED1.anode, J1.pin1, C1.1, C2.0, U3.GND
  N10: U1.RESET, S7.4, R3.Pin_0
  N11: U1.D2, S6.4
  N12: U1.D4, S5.2
  N13: U1.D7, S3.2
  N14: U1.D8, S2.4
  N15: U1.D9_(PWM), S4.2
  N16: U1.D10_(PWM), U3.CS
  N17: U1.D12, U3.MISO
  N18: LED1.cathode, R2.Pin_0
  N19: R2.Pin_1, U3.3.3

custom parts:
  : Nokia 5110 LCD with 8 pin. It's a 45mm*45mm module part. Description: The Nokia 5110 is a basic graphic LCD screen for lots of applications. It was originally intended for as a cell phone screen. This one is mounted on an easy to solder PCB. It uses the PCD8544 controller. The PCD8544 is a low power CMOS LCD controller/driver, designed to drive a graphic display of 48 rows and 84 columns. All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
  Ebay Breakout Board for SD Cards: Breakout Board for SD-MMC Cards
