# Fritzing sketch Nanobuino_shield (saved by Fritzing 0.8.7b)
circuit board: 5.64444cm x 8.46667cm
perfboards: 2

parts:
  Nokia_5110_LCD_Module2 = Nokia5110LCDModule  # not connected
  R3 = Resistor [tolerance=±5% resistance=220 package=THT]
  LED2 = LED - 3mm [color="Red (660nm)" package="3 mm [THT]"]
  LCD_CE_PULLUP1 = Resistor [tolerance=±5% resistance=10k package=THT]  # not connected
  U4 = Ebay Breakout Board for SD Cards
  BTN_0_(UP) = Momentary Switch [package=ksa_sealed_tac_switch]
  S8 = Momentary Switch [package=ksa_sealed_tac_switch]
  S9 = Momentary Switch [package=ksa_sealed_tac_switch]
  BTN_C1 = Momentary Switch [package=ksa_sealed_tac_switch]
  BTN2_(DOWN) = Momentary Switch [package=ksa_sealed_tac_switch]
  BTN1_(RIGHT) = Momentary Switch [package=ksa_sealed_tac_switch]
  BTN3_(LEFT) = Momentary Switch [package=ksa_sealed_tac_switch]
  KB2MB_L = female pin header, 8 pins [form="♀ (female)"]  # not connected
  J7 = Piezo Speaker
  LCD_CE_PULLUP = Resistor [tolerance=±5% resistance=10k package=THT]
  Part1 = Arduino Nano (Rev3.0)
  KB2MB_L1 = female pin header, 8 pins [form="♀ (female)"]  # not connected
  MB2LCD = female pin header, 16 pins [form="♀ (female)"]
  KB2MB_R = female pin header, 10 pins [form="♀ (female)"]
  KB2MB_R1 = female pin header, 10 pins [form="♀ (female)"]
  U5 = mystery part, 12 pins [chip_label="PAM8403 AMP BOARD"]

nets:
  N1: R3.Pin_0, LED2.cathode
  N2: R3.Pin_1, U4.GND#8
  N3: LED2.anode, U4.3.3
  N4: U4.GND#0, MB2LCD.pin12
  N5: U4.+5, MB2LCD.pin10, MB2LCD.pin11
  N6: U4.MOSI, MB2LCD.pin8
  N7: U4.SCK, MB2LCD.pin9
  N8: BTN_0_(UP).1, KB2MB_R.pin4, KB2MB_R1.pin4
  N9: BTN_0_(UP).3, S8.1, S9.1, BTN_C1.1, BTN1_(RIGHT).3
  N10: BTN_0_(UP).4, BTN3_(LEFT).1
  N11: S8.2, KB2MB_R.pin1, U5.pin11
  N12: S8.4, KB2MB_R.pin8, KB2MB_R1.pin8
  N13: S9.2, KB2MB_R.pin9, KB2MB_R1.pin9
  N14: BTN_C1.4, KB2MB_R.pin10, KB2MB_R1.pin10
  N15: BTN2_(DOWN).2, KB2MB_R.pin7, KB2MB_R1.pin7
  N16: BTN2_(DOWN).3, BTN3_(LEFT).2
  N17: BTN1_(RIGHT).2, KB2MB_R.pin6, KB2MB_R1.pin6
  N18: BTN3_(LEFT).4, KB2MB_R.pin5, KB2MB_R1.pin5
  N19: J7.pin1, U5.pin2
  N20: J7.pin2, U5.pin1
  N21: LCD_CE_PULLUP.Pin_0, KB2MB_R.pin2, KB2MB_R1.pin2
  N22: LCD_CE_PULLUP.Pin_1, Part1.A1
  N23: KB2MB_R.pin3, KB2MB_R1.pin3, U5.pin10, U5.pin12

notes:
  leftmost pin of display goes on top of pink wire on mainboard

custom parts:
  : Nokia 5110 LCD with 8 pin. It's a 45mm*45mm module part. Description: The Nokia 5110 is a basic graphic LCD screen for lots of applications. It was originally intended for as a cell phone screen. This one is mounted on an easy to solder PCB. It uses the PCD8544 controller. The PCD8544 is a low power CMOS LCD controller/driver, designed to drive a graphic display of 48 rows and 84 columns. All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
  Ebay Breakout Board for SD Cards: Breakout Board for SD-MMC Cards
